// Logisim project TTL-Computer.circ as structural Verilog
module Program_Counter (
);

  // _74191 74191_1: pin names not known
  // _74191 74191_2: pin names not known
  // _74191 74191_3: pin names not known
  // _74191 74191_4: pin names not known
endmodule

module Sequencer_Instruction_Decoder (
  input  _7,
  input  _6,
  input  _5,
  input  _4,
  input  _3,
  input  _2,
  input  _1,
  input  _0,
  input  nOE,
  input  RESTART,
  input  LOAD
);

  wire and_1_out, and_2_out, and_4_out, and_5_out, and_6_out, and_7_out, CLOCK_out, dip_74161_1_p1,
       dip_74161_1_p3, dip_74161_1_p5, dip_74161_1_p7, dip_74161_1_p9, dip_74161_1_p13, dip_74161_2_p9,
       dip_74161_2_p13, dip_74595_1_p1, dip_74595_1_p2, dip_74595_1_p3, dip_74595_1_p5, dip_74595_1_p6,
       dip_74595_1_p7, dip_74595_1_p9, dip_74595_1_p10, dip_74595_1_p11, dip_74595_1_p12, dip_74595_1_p13,
       dip_74595_1_p15, dip_74595_1_p17, dip_74595_2_p1, dip_74595_2_p3, dip_74595_2_p5, dip_74595_2_p6,
       dip_74595_2_p7, dip_74595_2_p8, dip_74595_2_p9, dip_74595_2_p11, dip_74595_2_p13, dip_74595_3_p1,
       dip_74595_3_p3, dip_74595_3_p5, dip_74595_3_p7, dip_74595_3_p8, dip_74595_3_p9, n74165_1_p1,
       n74165_1_p2, n74165_1_p13, not_1_out, not_3_out, not_4_out, not_5_out, or_1_out, or_2_out;
  wire [2:0] dip_74161_2_p3;
  wire [7:0] rom_1_data;

  ROM #(.addrWidth(19)) rom_1 (.addr({{16{1'b0}}, dip_74161_2_p3}), .data(rom_1_data), .sel(1'b1));
  // _74165 74165_1: pin names not known; wires that end beside it: n74165_1_p1, n74165_1_p2, _4, _5, _6, _7, 1'b0, _3, _2, _1, _0, 1'b0, n74165_1_p13
  nor nor_1 (n74165_1_p1, LOAD, and_1_out);
  LED led_1 (.in(n74165_1_p13));
  and and_1 (and_1_out, and_5_out, CLOCK_out);
  DotMatrix #(.matrixcols(24), .matrixrows(1), .dotshape("circle")) dotmatrix_1 (
    .col0(dip_74595_1_p1), .col1(dip_74595_1_p3), .col2(dip_74595_1_p5), .col3(dip_74595_1_p7),
    .col4(dip_74595_1_p9), .col5(dip_74595_1_p11), .col6(dip_74595_1_p13), .col7(dip_74595_1_p12),
    .col8(dip_74595_1_p15), .col9(dip_74595_1_p17), .col10(dip_74595_2_p1), .col11(dip_74595_2_p3),
    .col12(dip_74595_2_p5), .col13(dip_74595_2_p7), .col14(dip_74595_2_p9), .col15(dip_74595_2_p8),
    .col16(dip_74595_2_p11), .col17(dip_74595_2_p13), .col18(dip_74595_3_p1), .col19(dip_74595_3_p3),
    .col20(dip_74595_3_p5), .col21(dip_74595_3_p7), .col22(dip_74595_3_p9), .col23(dip_74595_3_p8));
  // DIP_74595 dip_74595_1: pin names not known; wires that end beside it: dip_74595_1_p1, dip_74595_1_p2, dip_74595_1_p3, n74165_1_p2, dip_74595_1_p5, dip_74595_1_p6, dip_74595_1_p7, nOE, dip_74595_1_p9, dip_74595_1_p10, dip_74595_1_p11, dip_74595_1_p12, dip_74595_1_p13, dip_74595_1_p10, dip_74595_1_p15, dip_74595_1_p2, dip_74595_1_p17, n74165_1_p2
  nor nor_2 (dip_74595_1_p2, n74165_1_p1, or_1_out);
  or or_1 (or_1_out, and_5_out, not_1_out);
  and and_2 (and_2_out, or_2_out, CLOCK_out);
  or or_2 (or_2_out, n74165_1_p1, and_5_out);
  not not_1 (not_1_out, CLOCK_out);
  Clock CLOCK (.out(CLOCK_out));
  // DIP_74595 dip_74595_2: pin names not known; wires that end beside it: dip_74595_2_p1, dip_74595_1_p6, dip_74595_2_p3, nOE, dip_74595_2_p5, dip_74595_2_p6, dip_74595_2_p7, dip_74595_2_p8, dip_74595_2_p9, dip_74595_2_p6, dip_74595_2_p11, dip_74595_1_p2, dip_74595_2_p13, n74165_1_p2
  not not_2 (dip_74595_1_p6, n74165_1_p2);
  and and_3 (n74165_1_p2, and_2_out, not_3_out);
  not not_3 (not_3_out, and_4_out);
  and and_4 (and_4_out, and_7_out, not_4_out);
  // DIP_74595 dip_74595_3: pin names not known; wires that end beside it: dip_74595_3_p1, dip_74595_1_p6, dip_74595_3_p3, nOE, dip_74595_3_p5, n74165_1_p13, dip_74595_3_p7, dip_74595_3_p8, dip_74595_3_p9
  not not_4 (not_4_out, LOAD);
  DotMatrix #(.matrixcols(4), .matrixrows(1), .dotshape("circle")) dotmatrix_2 (
    .col0(dip_74161_1_p9), .col1(dip_74161_1_p7), .col2(dip_74161_1_p5), .col3(dip_74161_1_p3));
  and and_5 (and_5_out, dip_74161_1_p3, dip_74161_1_p5, dip_74161_1_p7);
  // DIP_74161 dip_74161_1: pin names not known; wires that end beside it: dip_74161_1_p1, n74165_1_p2, dip_74161_1_p3, 1'b0, dip_74161_1_p5, 1'b0, dip_74161_1_p7, 1'b0, dip_74161_1_p9, 1'b0, 1'b1, 1'b1, dip_74161_1_p13
  or or_3 (dip_74161_1_p1, and_5_out, n74165_1_p1);
  not not_5 (not_5_out, dip_74595_1_p2);
  not not_6 (dip_74161_1_p13, and_5_out);
  and and_6 (and_6_out, and_5_out, n74165_1_p2);
  DotMatrix #(.matrixcols(4), .matrixrows(1), .dotshape("circle")) dotmatrix_3 (
    .col0(dip_74161_2_p9), .col1(dip_74161_2_p3[2]), .col2(dip_74161_2_p3[1]), .col3(dip_74161_2_p3[0]));
  // DIP_74161 dip_74161_2: pin names not known; wires that end beside it: not_5_out, and_6_out, dip_74161_2_p3[0], 1'b0, dip_74161_2_p3[1], 1'b0, dip_74161_2_p3[2], 1'b0, dip_74161_2_p9, 1'b0, 1'b1, 1'b1, dip_74161_2_p13
  not not_7 (dip_74161_2_p13, RESTART);
  and and_7 (and_7_out, dip_74161_2_p3[0], dip_74161_2_p3[1]);

  // Notes on the sheet:
  //   nOE: pull=down
  //   LOAD: pull=down
  //   RESTART: pull=down
  //   ROM DATA
  //   contents of rom_1 (hex, n*v repeats v):
  //   aa cc ff
  //   ROM DATA
  //   SH/~LR
  //   DATA
  //   NEXT_BIT
  //   ~CLR
  //   SHIFT REGISTER DATA
  //   RCLK
  //   SRCLK
  //   DONE
  //   DATA
  //   CLR
  //   NEXT_BIT
  //   DATA BIT COUNTER
  //   CE
  //   RESTART
  //   CLR
  //   DATA BYTE COUNTER
  //   CE
endmodule
